// Logisim project main.circ as structural Verilog: 5 circuits, main circuit main
module main (
  input  [4:0] chipId,
  input  [4:0] ballX,
  input  [4:0] ballY,
  input  [4:0] leftBatY,
  input  [4:0] rightBatY
);

  wire [4:0] videosection_1_out_14, videosection_1_out_15, videosection_1_out_16, videosection_1_out_17,
       videosection_1_out_18, videosection_2_out_14, videosection_2_out_15, videosection_2_out_16,
       videosection_2_out_17, videosection_2_out_18, videosection_3_out_14, videosection_3_out_15,
       videosection_3_out_16, videosection_3_out_17, videosection_3_out_18;
  wire [31:0] videosection_1_out_6, videosection_1_out_7, videosection_1_out_8, videosection_1_out_9,
       videosection_1_out_10, videosection_1_out_11, videosection_1_out_12, videosection_1_out_13,
       videosection_2_out_6, videosection_2_out_7, videosection_2_out_8, videosection_2_out_9,
       videosection_2_out_10, videosection_2_out_11, videosection_2_out_12, videosection_2_out_13,
       videosection_3_out_6, videosection_3_out_7, videosection_3_out_8, videosection_3_out_9,
       videosection_3_out_10, videosection_3_out_11, videosection_3_out_12, videosection_3_out_13,
       videosection_4_out_6, videosection_4_out_7, videosection_4_out_8, videosection_4_out_9,
       videosection_4_out_10, videosection_4_out_11, videosection_4_out_12, videosection_4_out_13;

  DotMatrix #(.matrixcols(32), .matrixrows(32)) dotmatrix_1 (
    .col0(videosection_1_out_10), .col1(videosection_1_out_6), .col2(videosection_1_out_11),
    .col3(videosection_1_out_7), .col4(videosection_1_out_12), .col5(videosection_1_out_8),
    .col6(videosection_1_out_13), .col7(videosection_1_out_9), .col8(videosection_2_out_10),
    .col9(videosection_2_out_6), .col10(videosection_2_out_11), .col11(videosection_2_out_7),
    .col12(videosection_2_out_12), .col13(videosection_2_out_8), .col14(videosection_2_out_13),
    .col15(videosection_2_out_9), .col16(videosection_3_out_10), .col17(videosection_3_out_6),
    .col18(videosection_3_out_11), .col19(videosection_3_out_7), .col20(videosection_3_out_12),
    .col21(videosection_3_out_8), .col22(videosection_3_out_13), .col23(videosection_3_out_9),
    .col24(videosection_4_out_10), .col25(videosection_4_out_6), .col26(videosection_4_out_11),
    .col27(videosection_4_out_7), .col28(videosection_4_out_12), .col29(videosection_4_out_8),
    .col30(videosection_4_out_13), .col31(videosection_4_out_9));
  videoSection videosection_1 (
    .chipID(chipId), .ballX(ballX), .ballY(ballY), .leftbatY(leftBatY), .rightbatY(rightBatY),
    .out_14(videosection_1_out_14), .out_15(videosection_1_out_15), .out_16(videosection_1_out_16),
    .out_17(videosection_1_out_17), .out_18(videosection_1_out_18), .out_10(videosection_1_out_10),
    .out_6(videosection_1_out_6), .out_11(videosection_1_out_11), .out_7(videosection_1_out_7),
    .out_12(videosection_1_out_12), .out_8(videosection_1_out_8), .out_13(videosection_1_out_13),
    .out_9(videosection_1_out_9));
  videoSection videosection_2 (
    .chipID(videosection_1_out_14), .ballX(videosection_1_out_15), .ballY(videosection_1_out_16),
    .leftbatY(videosection_1_out_17), .rightbatY(videosection_1_out_18), .out_14(videosection_2_out_14),
    .out_15(videosection_2_out_15), .out_16(videosection_2_out_16), .out_17(videosection_2_out_17),
    .out_18(videosection_2_out_18), .out_10(videosection_2_out_10), .out_6(videosection_2_out_6),
    .out_11(videosection_2_out_11), .out_7(videosection_2_out_7), .out_12(videosection_2_out_12),
    .out_8(videosection_2_out_8), .out_13(videosection_2_out_13), .out_9(videosection_2_out_9));
  videoSection videosection_3 (
    .chipID(videosection_2_out_14), .ballX(videosection_2_out_15), .ballY(videosection_2_out_16),
    .leftbatY(videosection_2_out_17), .rightbatY(videosection_2_out_18), .out_14(videosection_3_out_14),
    .out_15(videosection_3_out_15), .out_16(videosection_3_out_16), .out_17(videosection_3_out_17),
    .out_18(videosection_3_out_18), .out_10(videosection_3_out_10), .out_6(videosection_3_out_6),
    .out_11(videosection_3_out_11), .out_7(videosection_3_out_7), .out_12(videosection_3_out_12),
    .out_8(videosection_3_out_8), .out_13(videosection_3_out_13), .out_9(videosection_3_out_9));
  videoSection videosection_4 (
    .chipID(videosection_3_out_14), .ballX(videosection_3_out_15), .ballY(videosection_3_out_16),
    .leftbatY(videosection_3_out_17), .rightbatY(videosection_3_out_18), .out_10(videosection_4_out_10),
    .out_6(videosection_4_out_6), .out_11(videosection_4_out_11), .out_7(videosection_4_out_7),
    .out_12(videosection_4_out_12), .out_8(videosection_4_out_8), .out_13(videosection_4_out_13),
    .out_9(videosection_4_out_9));  // open: out_14, out_15, out_16, out_17, out_18

  // Notes on the sheet:
  //   test coords
endmodule

module videoSection (
  input  [4:0] chipID,
  input  [4:0] ballX,
  input  [4:0] ballY,
  input  [4:0] leftbatY,
  input  [4:0] rightbatY,
  output [31:0] out_6,
  output [31:0] out_7,
  output [31:0] out_8,
  output [31:0] out_9,
  output [31:0] out_10,
  output [31:0] out_11,
  output [31:0] out_12,
  output [31:0] out_13,
  output [4:0] out_14,
  output [4:0] out_15,
  output [4:0] out_16,
  output [4:0] out_17,
  output [4:0] out_18
);

  wire [4:0] videochip_1_out_7, videochip_1_out_8, videochip_1_out_9, videochip_1_out_10, videochip_1_out_11,
       videochip_2_out_7, videochip_2_out_8, videochip_2_out_9, videochip_2_out_10, videochip_2_out_11,
       videochip_3_out_7, videochip_3_out_8, videochip_3_out_9, videochip_3_out_10, videochip_3_out_11,
       videochip_4_out_7, videochip_4_out_8, videochip_4_out_9, videochip_4_out_10, videochip_4_out_11,
       videochip_5_out_7, videochip_5_out_8, videochip_5_out_9, videochip_5_out_10, videochip_5_out_11,
       videochip_6_out_7, videochip_6_out_8, videochip_6_out_9, videochip_6_out_10, videochip_6_out_11,
       videochip_7_out_7, videochip_7_out_8, videochip_7_out_9, videochip_7_out_10, videochip_7_out_11;

  videoChip videochip_1 (
    .chipID(chipID), .ballX(ballX), .ballY(ballY), .leftbatY(leftbatY), .rightbatY(rightbatY), .out(out_10),
    .out_10(videochip_1_out_10), .out_11(videochip_1_out_11), .out_9(videochip_1_out_9),
    .out_8(videochip_1_out_8), .out_7(videochip_1_out_7));
  videoChip videochip_2 (
    .chipID(videochip_3_out_10), .ballX(videochip_3_out_7), .ballY(videochip_3_out_8),
    .leftbatY(videochip_3_out_9), .rightbatY(videochip_3_out_11), .out(out_11), .out_10(videochip_2_out_10),
    .out_11(videochip_2_out_11), .out_9(videochip_2_out_9), .out_8(videochip_2_out_8),
    .out_7(videochip_2_out_7));
  videoChip videochip_3 (
    .chipID(videochip_1_out_10), .ballX(videochip_1_out_7), .ballY(videochip_1_out_8),
    .leftbatY(videochip_1_out_9), .rightbatY(videochip_1_out_11), .out(out_6), .out_10(videochip_3_out_10),
    .out_11(videochip_3_out_11), .out_9(videochip_3_out_9), .out_8(videochip_3_out_8),
    .out_7(videochip_3_out_7));
  videoChip videochip_4 (
    .chipID(videochip_2_out_10), .ballX(videochip_2_out_7), .ballY(videochip_2_out_8),
    .leftbatY(videochip_2_out_9), .rightbatY(videochip_2_out_11), .out(out_7), .out_10(videochip_4_out_10),
    .out_11(videochip_4_out_11), .out_9(videochip_4_out_9), .out_8(videochip_4_out_8),
    .out_7(videochip_4_out_7));
  videoChip videochip_5 (
    .chipID(videochip_4_out_10), .ballX(videochip_4_out_7), .ballY(videochip_4_out_8),
    .leftbatY(videochip_4_out_9), .rightbatY(videochip_4_out_11), .out(out_12), .out_10(videochip_5_out_10),
    .out_11(videochip_5_out_11), .out_9(videochip_5_out_9), .out_8(videochip_5_out_8),
    .out_7(videochip_5_out_7));
  videoChip videochip_6 (
    .chipID(videochip_7_out_10), .ballX(videochip_7_out_7), .ballY(videochip_7_out_8),
    .leftbatY(videochip_7_out_9), .rightbatY(videochip_7_out_11), .out(out_13), .out_10(videochip_6_out_10),
    .out_11(videochip_6_out_11), .out_9(videochip_6_out_9), .out_8(videochip_6_out_8),
    .out_7(videochip_6_out_7));
  videoChip videochip_7 (
    .chipID(videochip_5_out_10), .ballX(videochip_5_out_7), .ballY(videochip_5_out_8),
    .leftbatY(videochip_5_out_9), .rightbatY(videochip_5_out_11), .out(out_8), .out_10(videochip_7_out_10),
    .out_11(videochip_7_out_11), .out_9(videochip_7_out_9), .out_8(videochip_7_out_8),
    .out_7(videochip_7_out_7));
  videoChip videochip_8 (
    .chipID(videochip_6_out_10), .ballX(videochip_6_out_7), .ballY(videochip_6_out_8),
    .leftbatY(videochip_6_out_9), .rightbatY(videochip_6_out_11), .out(out_9), .out_10(out_14),
    .out_11(out_18), .out_9(out_17), .out_8(out_16), .out_7(out_15));
endmodule

module videoChip (
  input  [4:0] chipID,
  input  [4:0] ballX,
  input  [4:0] ballY,
  input  [4:0] leftbatY,
  input  [4:0] rightbatY,
  output [31:0] out,
  output [4:0] out_7,
  output [4:0] out_8,
  output [4:0] out_9,
  output [4:0] out_10,
  output [4:0] out_11
);

  wire [31:0] cmpchipball_1_out, cmpchipball_2_out, cmpchipball_3_out, or_1_out, shifter_1_out, shifter_2_out;

  cmpChipBall cmpchipball_1 (.chipId(chipID), .ballX(ballX), .ballY(ballY), .out(cmpchipball_1_out));
  cmpChipBall cmpchipball_2 (.chipId(chipID), .ballX(5'b00011), .ballY(leftbatY), .out(cmpchipball_2_out));
  cmpChipBall cmpchipball_3 (.chipId(chipID), .ballX(5'b11100), .ballY(rightbatY), .out(cmpchipball_3_out));
  Adder #(.width(5)) adder_1 (.a(5'b00001), .b(chipID), .out(out_10));  // open: cin, cout
  assign or_1_out = cmpchipball_2_out | cmpchipball_3_out;  // OR_Gate or_1, 32 bits wide
  Shifter #(.width(32)) shifter_1 (.in(or_1_out), .\dist (5'b00010), .out(shifter_1_out));
  Shifter #(.width(32)) shifter_2 (.in(or_1_out), .\dist (5'b00001), .out(shifter_2_out));
  assign out = cmpchipball_1_out | or_1_out | shifter_1_out | shifter_2_out;  // OR_Gate or_2, 32 bits wide

  assign out_7 = ballX;
  assign out_8 = ballY;
  assign out_9 = leftbatY;
  assign out_11 = rightbatY;

  // Other names for the same wires on the sheet: lBatY[4:0] = leftbatY; rBatY[4:0] = rightbatY
endmodule

module cmpChipBall (
  input  [4:0] ballY,
  input  [4:0] chipId,
  input  [4:0] ballX,
  output [31:0] out
);

  wire comparator_1_eq;

  // Probe on out
  Decoder #(.select(5), .disabled(0)) decoder_1 (
    .out0(out[0]), .out1(out[1]), .out2(out[2]), .out3(out[3]), .out4(out[4]), .out5(out[5]), .out6(out[6]),
    .out7(out[7]), .out8(out[8]), .out9(out[9]), .out10(out[10]), .out11(out[11]), .out12(out[12]),
    .out13(out[13]), .out14(out[14]), .out15(out[15]), .out16(out[16]), .out17(out[17]), .out18(out[18]),
    .out19(out[19]), .out20(out[20]), .out21(out[21]), .out22(out[22]), .out23(out[23]), .out24(out[24]),
    .out25(out[25]), .out26(out[26]), .out27(out[27]), .out28(out[28]), .out29(out[29]), .out30(out[30]),
    .out31(out[31]), .sel(ballY), .en(comparator_1_eq));
  Comparator #(.width(5)) comparator_1 (.a(chipId), .b(ballX), .eq(comparator_1_eq));  // open: gt, lt
endmodule

module mine (
  input  [7:0] bus_0,
  input  [7:0] bus_0_2,
  input  [7:0] bus_1,
  input  [7:0] bus_1_2,
  input  [7:0] bus_2,
  input  [7:0] bus_3,
  input  bus_0_3,
  input  [1:0] bus_0_4,
  input  [2:0] bus_0_5,
  input  S,
  input  R,
  input  S_2,
  input  R_2,
  output Q,
  output Q_prime,
  output Q_prime_2,
  output Q_2
);

  wire clock_1_out;
  wire [7:0] decoder_1_out0, multiplexer_1_out, multiplexer_2_out;

  Decoder #(.select(3), .disabled(0)) decoder_1 (
    .out0(decoder_1_out0[0]), .out1(decoder_1_out0[1]), .out2(decoder_1_out0[2]), .out3(decoder_1_out0[3]),
    .out4(decoder_1_out0[4]), .out5(decoder_1_out0[5]), .out6(decoder_1_out0[6]), .out7(decoder_1_out0[7]),
    .sel(bus_0_5));  // open: en
  nor nor_1 (Q_prime_2, S_2, Q_2);
  nor nor_2 (Q_2, Q_prime_2, R_2);
  Multiplexer #(.select(2), .width(8)) multiplexer_1 (
    .in0(bus_0), .in1(bus_1), .in2(bus_2), .in3(bus_3), .out(multiplexer_1_out), .sel(bus_0_4));  // open: en
  // Probe on multiplexer_1_out
  // Probe on decoder_1_out0
  // Probe on decoder_1_out0
  Clock clock_1 (.out(clock_1_out));
  S_R_Flip_Flop s_r_ff_1 (.S(S), .clk(clock_1_out), .R(R), .Q(Q), .Qn(Q_prime));  // open: preset, reset, en
  Multiplexer #(.width(8)) multiplexer_2 (
    .in0(bus_0_2), .in1(bus_1_2), .out(multiplexer_2_out), .sel(bus_0_3));  // open: en
  // Probe on multiplexer_2_out

  // Notes on the sheet:
  //   216
  //   RS flip-flop
  //   S R Q` Q
  //   1  0  0  1
  //   0  1  1  0
  //   1  1  0  0
  //   0  0  1  0 or 0  0  0  1
endmodule
